# Fritzing sketch ir-clone-test-setup (saved by Fritzing 0.9.3b)

parts:
  M1 = IR Cloner [part_number=KT0004 package=THT]
  Generic_4x4_button_keypad1 = Generic 4x4 Keypad

nets:
  N1: M1.KB1, Generic_4x4_button_keypad1.R4
  N2: M1.KB2, Generic_4x4_button_keypad1.R3
  N3: M1.KB3, Generic_4x4_button_keypad1.R2
  N4: M1.KB4, Generic_4x4_button_keypad1.R1
  N5: M1.KB5, Generic_4x4_button_keypad1.C1
  N6: M1.KB6, Generic_4x4_button_keypad1.C2
  N7: M1.KB7, Generic_4x4_button_keypad1.C3
  N8: M1.KB8, Generic_4x4_button_keypad1.C4
  N9: M1.NC4, M1.NC5

notes:
  GND
  +5V
  Input from +5V DC Power Supply
  4 x 4 Matrix Keypad
  Short Pin 1 and 2 of JP101

custom parts:
  IR Cloner: IR Remote Control Clone Utility
  Generic 4x4 Keypad: generic 4x4 keypad 4 rows of four 6 mm tact switches cheap and nasty but works
